# Fritzing sketch GreenPi (saved by Fritzing 0.8.0b)
breadboards: 1

parts:
  IC1 = IC, DIP package, 16 pins [chip_label=MCP3008]
  J1 = screw terminal, 2 pins
  R2 = Photocell (LDR) [package=THT]
  LED1 = LED - 5mm [color="Red (633nm)" package="5 mm [THT]"]
  R1 = Rotary Potentiometer (Small) [maximum_resistance=10kΩ]
  T1 = TMP36 Temperature Sensor [package="TO92 [THT]"]
  Raspberry_Pi1 = Raspberry Pi
  R4 = Resistor [tolerance=±5% resistance=220 package=THT]
  test_pins = male pin header, 5 pins [form="♂ (male)"]
  R5 = Resistor [tolerance=±5% resistance=100k package=THT]
  ext_points = female pin header, 5 pins [form="♀ (female)"]

nets:
  N1: IC1.pin1, R2.pin_0, test_pins.pin5, R5.Pin_1
  N2: IC1.pin2, J1.pin1, R1.leg2, test_pins.pin4
  N3: IC1.pin3, T1.Vout, test_pins.pin3
  N4: IC1.pin4, ext_points.pin5
  N5: IC1.pin5, ext_points.pin4
  N6: IC1.pin6, ext_points.pin3
  N7: IC1.pin7, ext_points.pin2
  N8: IC1.pin8, ext_points.pin1
  GND: IC1.pin9, IC1.pin14, R1.wiper, T1.GND, Raspberry_Pi1.GND, R4.Pin_0, test_pins.pin2, R5.Pin_0
  N9: IC1.pin10, Raspberry_Pi1.SPI_CE0_N
  N10: IC1.pin11, Raspberry_Pi1.SPI_SCLK
  N11: IC1.pin12, Raspberry_Pi1.SPI_MISO
  N12: IC1.pin13, Raspberry_Pi1.SPI_MOSI
  3.3V: IC1.pin15, IC1.pin16, J1.pin2, R2.pin_1, T1.+Vs, Raspberry_Pi1.3V3, test_pins.pin1
  N13: LED1.cathode, R4.Pin_1
  N14: LED1.anode, Raspberry_Pi1.GPIO7

notes:
  +
  lum
  moisture
  temp
  3v3
  gnd
